// Logisim project Ctl_Shift_Add_Sub_Mov.circ as structural Verilog: 1 circuit, main circuit Shift_Add_Sub_Mov
module Shift_Add_Sub_Mov (
  input  [15:0] Instruction,
  input  Enable,
  output [2:0] Rn,
  output [31:0] Imm32,
  output [2:0] Rm,
  output [4:0] Imm5,
  output [2:0] Rd,
  output Carry,
  output [3:0] ALU_Opcode,
  output [3:0] Flags_Update_Mask,
  output Imm32_Enable
);

  wire and_2_out;
  wire [15:0] bit_extender_1_out, Instr;

  assign bit_extender_1_out = {{15{Enable}}, Enable};  // Bit_Extender bit_extender_1
  Multiplexer #(.select(3), .width(4)) multiplexer_1 (
    .in0(4'b1100), .in1(4'b1100), .in2(4'b1100), .in3(4'b1100), .in4(4'b1100), .in5(4'b0000), .in6(4'b0000),
    .in7(4'b0000), .out(Flags_Update_Mask), .sel({Carry, ALU_Opcode[3:2]}));
  assign {Instr[15:14], Carry, ALU_Opcode, Rd[0], Instr[7:0]} = Instruction & bit_extender_1_out;  // AND_Gate and_1, 16 bits wide
  assign Imm32 = {{24{Instr[7]}}, Instr[7:0]};  // Bit_Extender bit_extender_2
  Multiplexer #(.width(3)) multiplexer_2 (.in0(Rn), .in1(Imm5[2:0]), .out(Rm), .sel(and_2_out));
  and and_2 (and_2_out, ALU_Opcode[2], ALU_Opcode[3], ~Carry);  // AND_Gate

  assign Imm32_Enable = 1'b0;
  assign Rd[2:1] = ALU_Opcode[1:0];

  // Other names for the same wires on the sheet: Instr[13:8] = {Carry, ALU_Opcode, Rd[0]};
  //   G[2:0] = {Carry, ALU_Opcode[3:2]}

  // Notes on the sheet:
  //   Pull output low on Enable = 0
  //   Note: ALU uses Rn register for shifts. Use Rn instead of Rm for shifts (immediate) here too
  //   Note 3: Imm32_Enable forces the use of the immediate for Rm register
  //   Note 2: MOV uses RSB ALU opcode with Imm8 reversed so that it is copied to output register
endmodule
